# Fritzing sketch board_connection (saved by Fritzing 1.0.0d)
breadboards: 1

parts:
  Part2 = Arduino Uno (Rev3)
  R1 = Photocell (LDR) [package=THT]
  R2 = Resistor [tolerance=±5% power=0.25W resistance=1000 package=THT]
  S1 = Pushbutton [package="[THT]"]
  S2 = Pushbutton [package="[THT]"]
  R3 = Resistor [tolerance=±5% power=0.25W resistance=1000 package=THT]
  LED1 = LED - 5mm [color="Red (633nm)" current=0.030A package="5 mm [THT]"]
  LED2 = LED - 5mm [color="Yellow (585nm)" current=0.030A package="5 mm [THT]"]
  R4 = Rotary Potentiometer (Small) [maximum_resistance=10kΩ knob_status=50% power=0.5W package=THT]
  R5 = Resistor [tolerance=±5% power=0.25W resistance=1000 package=THT]
  R6 = Resistor [tolerance=±5% power=0.25W resistance=330 package=THT]
  R7 = Resistor [tolerance=±5% power=0.25W resistance=330 package=THT]

nets:
  N1: Part2.A0, R1.pin_1, R2.Pin_0
  N2: Part2.A1, R4.wiper
  N3: Part2.D8, LED1.anode
  N4: Part2.D9_PWM, LED2.anode
  N5: Part2.D2, S1.Pin_1, S1.Pin_2, R3.Pin_0
  N6: Part2.D3_PWM, S2.Pin_1, S2.Pin_2, R5.Pin_0
  N7: Part2.5V, R2.Pin_1, R4.leg2
  N8: Part2.GND, R1.pin_0, R4.leg1
  N9: S1.Pin_3, S1.Pin_4, S2.Pin_3, S2.Pin_4, R6.Pin_1, R7.Pin_1
  N10: R3.Pin_1, R5.Pin_1
  N11: LED1.cathode, R6.Pin_0
  N12: LED2.cathode, R7.Pin_0
